// Logisim project stack_logisim_.circ as structural Verilog: 16 circuits, main circuit main
module main (
  input  [2:0] INDEX,
  input  [3:0] I_DATA,
  input  [1:0] COMMAND,
  input  CLK,
  input  RESET,
  output [3:0] O_DATA
);

  stack stack_1 (.INDEX(INDEX), .I_DATA(I_DATA), .COMMAND(COMMAND), .CLK(CLK), .RESET(RESET), .O_DATA(O_DATA));
endmodule

module jk_trig (
  input  J,
  input  C,
  input  K,
  output y1,
  output y2
);

  wire nand_1_out, nand_2_out, nand_4_out, por_1_out;

  nand nand_1 (nand_1_out, J, C);
  nand nand_2 (nand_2_out, C, K);
  nand nand_3 (y1, nand_1_out, y2);
  nand nand_4 (nand_4_out, y1, nand_2_out);
  POR por_1 (.out(por_1_out));
  or or_1 (y2, nand_4_out, por_1_out);
endmodule

module d_trig (
  input  D,
  input  clk,
  output out_3,
  output out_4
);

  wire not_1_out;

  not not_1 (not_1_out, D);
  jk_trig jk_trig_1 (.J(D), .C(clk), .K(not_1_out), .y1(out_3), .y2(out_4));
endmodule

module add1mod5 (
  input  a0,
  input  a1,
  input  b,
  output y1,
  output y2
);

  wire and_1_out, and_2_out, xor_1_out;

  xor xor_1 (xor_1_out, a0, a1);
  xor xor_2 (y1, xor_1_out, b);
  and and_1 (and_1_out, xor_1_out, b);
  and and_2 (and_2_out, a0, a1);
  or or_1 (y2, and_1_out, and_2_out);
endmodule

module add3mod5 (
  input  in_1,
  input  in_2,
  input  in_3,
  input  in_4,
  input  in_5,
  input  in_6,
  output out_7,
  output out_8,
  output out_9
);

  wire add1mod5_1_y1, add1mod5_1_y2, add1mod5_2_y1, add1mod5_2_y2, add1mod5_3_y1, add1mod5_3_y2;

  add1mod5 add1mod5_1 (.a0(in_1), .a1(in_4), .b(1'b0), .y1(add1mod5_1_y1), .y2(add1mod5_1_y2));
  add1mod5 add1mod5_2 (.a0(in_2), .a1(in_5), .b(add1mod5_1_y2), .y1(add1mod5_2_y1), .y2(add1mod5_2_y2));
  add1mod5 add1mod5_3 (.a0(in_3), .a1(in_6), .b(add1mod5_2_y2), .y1(add1mod5_3_y1), .y2(add1mod5_3_y2));
  mod5_4bit mod5_4bit_1 (
    .q0(add1mod5_1_y1), .q1(add1mod5_2_y1), .q2(add1mod5_3_y1), .q3(add1mod5_3_y2), .out_5(out_7),
    .out_6(out_8), .out_7(out_9));

  // Notes on the sheet:
  //   сверху младшие биты
endmodule

module mem1 (
  input  x,
  input  clk,
  input  rst,
  output y
);

  wire mx2_1_1_y, or_1_out;

  mx2_1 mx2_1_1 (.x0(x), .x1(1'b0), .a(rst), .y(mx2_1_1_y));
  or or_1 (or_1_out, clk, rst);
  d_trig d_trig_1 (.D(mx2_1_1_y), .clk(or_1_out), .out_3(y));  // open: out_4
endmodule

module mx2_1 (
  input  x0,
  input  x1,
  input  a,
  output y
);

  wire and_1_out, and_2_out, not_1_out;

  not not_1 (not_1_out, a);
  and and_1 (and_1_out, x0, not_1_out);
  and and_2 (and_2_out, x1, a);
  or or_1 (y, and_1_out, and_2_out);
endmodule

module mem4 (
  input  in_1,
  input  in_2,
  input  in_3,
  input  in_4,
  input  wr,
  input  clk,
  input  rst,
  output out_8,
  output out_9,
  output out_10,
  output out_11
);

  wire and_1_out;

  and and_1 (and_1_out, wr, clk);
  mem1 mem1_1 (.x(in_1), .clk(and_1_out), .rst(rst), .y(out_8));
  mem1 mem1_2 (.x(in_2), .clk(and_1_out), .rst(rst), .y(out_9));
  mem1 mem1_3 (.x(in_3), .clk(and_1_out), .rst(rst), .y(out_10));
  mem1 mem1_4 (.x(in_4), .clk(and_1_out), .rst(rst), .y(out_11));
endmodule

module mem3 (
  input  in_1,
  input  in_2,
  input  in_3,
  input  clk,
  input  rst,
  output out_6,
  output out_7,
  output out_8
);

  mem1 mem1_1 (.x(in_1), .clk(clk), .rst(rst), .y(out_6));
  mem1 mem1_2 (.x(in_2), .clk(clk), .rst(rst), .y(out_7));
  mem1 mem1_3 (.x(in_3), .clk(clk), .rst(rst), .y(out_8));
endmodule

module dec3_5 (
  input  x1,
  input  x2,
  input  x3,
  output y1,
  output y2,
  output y3,
  output y4,
  output y5
);

  wire not_1_out, not_2_out, not_3_out;

  not not_1 (not_1_out, x1);
  not not_2 (not_2_out, x2);
  not not_3 (not_3_out, x3);
  and and_1 (y5, not_3_out, not_2_out, not_1_out);
  and and_2 (y4, not_3_out, not_2_out, x1);
  and and_3 (y3, not_3_out, x2, not_1_out);
  and and_4 (y2, not_3_out, x2, x1);
  and and_5 (y1, x3, not_2_out, not_1_out);
endmodule

module stack (
  input  [2:0] INDEX,
  input  [3:0] I_DATA,
  input  [1:0] COMMAND,
  input  CLK,
  input  RESET,
  output [3:0] O_DATA
);

  wire add3mod5_1_out_7, add3mod5_1_out_8, add3mod5_1_out_9, add3mod5_2_out_7, add3mod5_2_out_8,
       add3mod5_2_out_9, add3mod5_3_out_7, add3mod5_3_out_8, add3mod5_3_out_9, add3mod5_4_out_7,
       add3mod5_4_out_8, add3mod5_4_out_9, add3mod5_5_out_7, add3mod5_5_out_8, add3mod5_5_out_9, and_1_out,
       and_2_out, and_3_out, dec2_4_1_out_4, dec2_4_1_out_5, dec2_4_1_out_6, dec3_5_1_y1, dec3_5_1_y2,
       dec3_5_1_y3, dec3_5_1_y4, dec3_5_1_y5, dec3_5_2_y1, dec3_5_2_y2, dec3_5_2_y3, dec3_5_2_y4,
       dec3_5_2_y5, mem3_1_out_6, mem3_1_out_7, mem3_1_out_8, mem3_2_out_6, mem3_2_out_7, mem3_2_out_8,
       mem3_3_out_6, mem3_3_out_7, mem3_3_out_8, mem4_1_out_8, mem4_1_out_9, mem4_1_out_10, mem4_1_out_11,
       mem4_2_out_8, mem4_2_out_9, mem4_2_out_10, mem4_2_out_11, mem4_3_out_8, mem4_3_out_9, mem4_3_out_10,
       mem4_3_out_11, mem4_4_out_8, mem4_4_out_9, mem4_4_out_10, mem4_4_out_11, mem4_5_out_8, mem4_5_out_9,
       mem4_5_out_10, mem4_5_out_11, mod5min3_1_out_4, mod5min3_1_out_5, mod5min3_1_out_6, mx2_1_1_y,
       mx2_1_2_y, mx2_1_3_y, mx2_1_4_y, mx2_1_5_y, mx2_1_6_y, mx2_1_7_y, mx2_1_8_y, mx2_1_9_y, mx2_1_10_y,
       mx2_1_11_y, mx2_1_12_y, mx2_1_13_y, mx2_1_14_y, mx2_1_15_y, mx2_1_16_y, mx2_1_17_y, mx2_1_18_y,
       mx2_1_19_y, mx20_4_1_out_26, mx20_4_1_out_27, mx20_4_1_out_28, mx20_4_1_out_29, not_1_out, not_2_out,
       or_1_out, transmission_1_p4;

  and and_1 (and_1_out, CLK, dec2_4_1_out_5);
  not not_1 (not_1_out, CLK);
  add3mod5 add3mod5_1 (
    .in_1(INDEX[0]), .in_2(INDEX[1]), .in_3(INDEX[2]), .in_4(1'b0), .in_5(1'b0), .in_6(1'b0),
    .out_7(add3mod5_1_out_7), .out_8(add3mod5_1_out_8), .out_9(add3mod5_1_out_9));
  dec2_4 dec2_4_1 (
    .in_1(COMMAND[0]), .in_2(COMMAND[1]), .out_4(dec2_4_1_out_4), .out_5(dec2_4_1_out_5),
    .out_6(dec2_4_1_out_6));  // open: out_3
  and and_2 (and_2_out, CLK, dec2_4_1_out_6);
  mem3 mem3_1 (
    .in_1(mem3_3_out_6), .in_2(mem3_3_out_7), .in_3(mem3_3_out_8), .clk(CLK), .rst(RESET),
    .out_6(mem3_1_out_6), .out_7(mem3_1_out_7), .out_8(mem3_1_out_8));
  add3mod5 add3mod5_2 (
    .in_1(1'b1), .in_2(1'b0), .in_3(1'b0), .in_4(mem3_2_out_6), .in_5(mem3_2_out_7), .in_6(mem3_2_out_8),
    .out_7(add3mod5_2_out_7), .out_8(add3mod5_2_out_8), .out_9(add3mod5_2_out_9));
  and and_3 (and_3_out, dec2_4_1_out_4, CLK);
  mod5min3 mod5min3_1 (
    .in_1(add3mod5_1_out_7), .in_2(add3mod5_1_out_8), .in_3(add3mod5_1_out_9), .out_4(mod5min3_1_out_4),
    .out_5(mod5min3_1_out_5), .out_6(mod5min3_1_out_6));
  mem3 mem3_2 (
    .in_1(mem3_1_out_6), .in_2(mem3_1_out_7), .in_3(mem3_1_out_8), .clk(not_1_out), .rst(RESET),
    .out_6(mem3_2_out_6), .out_7(mem3_2_out_7), .out_8(mem3_2_out_8));
  add3mod5 add3mod5_3 (
    .in_1(mod5min3_1_out_4), .in_2(mod5min3_1_out_5), .in_3(mod5min3_1_out_6), .in_4(mem3_2_out_6),
    .in_5(mem3_2_out_7), .in_6(mem3_2_out_8), .out_7(add3mod5_3_out_7), .out_8(add3mod5_3_out_8),
    .out_9(add3mod5_3_out_9));
  dec3_5 dec3_5_1 (
    .x1(mem3_2_out_6), .x2(mem3_2_out_7), .x3(mem3_2_out_8), .y1(dec3_5_1_y1), .y2(dec3_5_1_y2),
    .y3(dec3_5_1_y3), .y4(dec3_5_1_y4), .y5(dec3_5_1_y5));
  add3mod5 add3mod5_4 (
    .in_1(1'b0), .in_2(1'b0), .in_3(1'b1), .in_4(mem3_2_out_6), .in_5(mem3_2_out_7), .in_6(mem3_2_out_8),
    .out_7(add3mod5_4_out_7), .out_8(add3mod5_4_out_8), .out_9(add3mod5_4_out_9));
  add3mod5 add3mod5_5 (
    .in_1(add3mod5_3_out_7), .in_2(add3mod5_3_out_8), .in_3(add3mod5_3_out_9), .in_4(1'b0), .in_5(1'b0),
    .in_6(1'b1), .out_7(add3mod5_5_out_7), .out_8(add3mod5_5_out_8), .out_9(add3mod5_5_out_9));
  dec3_5 dec3_5_2 (
    .x1(add3mod5_5_out_7), .x2(add3mod5_5_out_8), .x3(add3mod5_5_out_9), .y1(dec3_5_2_y1), .y2(dec3_5_2_y2),
    .y3(dec3_5_2_y3), .y4(dec3_5_2_y4), .y5(dec3_5_2_y5));
  mx2_1 mx2_1_1 (.x0(dec3_5_1_y1), .x1(dec3_5_2_y1), .a(and_2_out), .y(mx2_1_1_y));
  mx2_1 mx2_1_2 (.x0(dec3_5_1_y2), .x1(dec3_5_2_y2), .a(and_2_out), .y(mx2_1_2_y));
  mx2_1 mx2_1_3 (.x0(dec3_5_1_y3), .x1(dec3_5_2_y3), .a(and_2_out), .y(mx2_1_3_y));
  mx2_1 mx2_1_4 (.x0(dec3_5_1_y4), .x1(dec3_5_2_y4), .a(and_2_out), .y(mx2_1_4_y));
  mx2_1 mx2_1_5 (.x0(dec3_5_1_y5), .x1(dec3_5_2_y5), .a(and_2_out), .y(mx2_1_5_y));
  or or_1 (or_1_out, and_2_out, and_1_out);
  mx2_1 mx2_1_6 (.x0(mem3_2_out_6), .x1(add3mod5_4_out_7), .a(and_1_out), .y(mx2_1_6_y));
  mx2_1 mx2_1_7 (.x0(mem3_2_out_7), .x1(add3mod5_4_out_8), .a(and_1_out), .y(mx2_1_7_y));
  mx2_1 mx2_1_8 (.x0(mem3_2_out_8), .x1(add3mod5_4_out_9), .a(and_1_out), .y(mx2_1_8_y));
  mem4 mem4_1 (
    .in_1(I_DATA[0]), .in_2(I_DATA[1]), .in_3(I_DATA[2]), .in_4(I_DATA[3]), .wr(and_3_out), .clk(mx2_1_1_y),
    .rst(RESET), .out_8(mem4_1_out_8), .out_9(mem4_1_out_9), .out_10(mem4_1_out_10), .out_11(mem4_1_out_11));
  mem4 mem4_2 (
    .in_1(I_DATA[0]), .in_2(I_DATA[1]), .in_3(I_DATA[2]), .in_4(I_DATA[3]), .wr(and_3_out), .clk(mx2_1_2_y),
    .rst(RESET), .out_8(mem4_2_out_8), .out_9(mem4_2_out_9), .out_10(mem4_2_out_10), .out_11(mem4_2_out_11));
  mem4 mem4_3 (
    .in_1(I_DATA[0]), .in_2(I_DATA[1]), .in_3(I_DATA[2]), .in_4(I_DATA[3]), .wr(and_3_out), .clk(mx2_1_3_y),
    .rst(RESET), .out_8(mem4_3_out_8), .out_9(mem4_3_out_9), .out_10(mem4_3_out_10), .out_11(mem4_3_out_11));
  mem4 mem4_4 (
    .in_1(I_DATA[0]), .in_2(I_DATA[1]), .in_3(I_DATA[2]), .in_4(I_DATA[3]), .wr(and_3_out), .clk(mx2_1_4_y),
    .rst(RESET), .out_8(mem4_4_out_8), .out_9(mem4_4_out_9), .out_10(mem4_4_out_10), .out_11(mem4_4_out_11));
  mem4 mem4_5 (
    .in_1(I_DATA[0]), .in_2(I_DATA[1]), .in_3(I_DATA[2]), .in_4(I_DATA[3]), .wr(and_3_out), .clk(mx2_1_5_y),
    .rst(RESET), .out_8(mem4_5_out_8), .out_9(mem4_5_out_9), .out_10(mem4_5_out_10), .out_11(mem4_5_out_11));
  not not_2 (not_2_out, or_1_out);
  // Transmission_Gate transmission_1: pin names not known; wires that end beside it: or_1_out, not_2_out, or_1_out, transmission_1_p4
  mx2_1 mx2_1_9 (.x0(mx2_1_6_y), .x1(1'b0), .a(RESET), .y(mx2_1_9_y));
  mx2_1 mx2_1_10 (.x0(mx2_1_7_y), .x1(1'b0), .a(RESET), .y(mx2_1_10_y));
  mx2_1 mx2_1_11 (.x0(mx2_1_8_y), .x1(1'b0), .a(RESET), .y(mx2_1_11_y));
  mx2_1 mx2_1_12 (.x0(mx2_1_1_y), .x1(mx2_1_5_y), .a(and_1_out), .y(mx2_1_12_y));
  mx2_1 mx2_1_13 (.x0(mx2_1_2_y), .x1(mx2_1_1_y), .a(and_1_out), .y(mx2_1_13_y));
  mx2_1 mx2_1_14 (.x0(mx2_1_3_y), .x1(mx2_1_2_y), .a(and_1_out), .y(mx2_1_14_y));
  mx2_1 mx2_1_15 (.x0(mx2_1_4_y), .x1(mx2_1_3_y), .a(and_1_out), .y(mx2_1_15_y));
  mx2_1 mx2_1_16 (.x0(mx2_1_5_y), .x1(mx2_1_4_y), .a(and_1_out), .y(mx2_1_16_y));
  mx2_1 mx2_1_17 (.x0(mx2_1_9_y), .x1(add3mod5_2_out_7), .a(and_3_out), .y(mx2_1_17_y));
  mx2_1 mx2_1_18 (.x0(mx2_1_10_y), .x1(add3mod5_2_out_8), .a(and_3_out), .y(mx2_1_18_y));
  mx2_1 mx2_1_19 (.x0(mx2_1_11_y), .x1(add3mod5_2_out_9), .a(and_3_out), .y(mx2_1_19_y));
  mx20_4 mx20_4_1 (
    .in_1(mem4_1_out_8), .in_2(mem4_1_out_9), .in_3(mem4_1_out_10), .in_4(mem4_1_out_11),
    .in_5(mem4_2_out_8), .in_6(mem4_2_out_9), .in_7(mem4_2_out_10), .in_8(mem4_2_out_11),
    .in_9(mem4_3_out_8), .in_10(mem4_3_out_9), .in_11(mem4_3_out_10), .in_12(mem4_3_out_11),
    .in_13(mem4_4_out_8), .in_14(mem4_4_out_9), .in_15(mem4_4_out_10), .in_16(mem4_4_out_11),
    .in_17(mem4_5_out_8), .in_18(mem4_5_out_9), .in_19(mem4_5_out_10), .in_20(mem4_5_out_11),
    .in_21(mx2_1_12_y), .in_22(mx2_1_13_y), .in_23(mx2_1_14_y), .in_24(mx2_1_15_y), .in_25(mx2_1_16_y),
    .out_26(mx20_4_1_out_26), .out_27(mx20_4_1_out_27), .out_28(mx20_4_1_out_28), .out_29(mx20_4_1_out_29));
  mem3 mem3_3 (
    .in_1(mx2_1_17_y), .in_2(mx2_1_18_y), .in_3(mx2_1_19_y), .clk(CLK), .rst(RESET), .out_6(mem3_3_out_6),
    .out_7(mem3_3_out_7), .out_8(mem3_3_out_8));
  mx2_1 mx2_1_20 (.x1(mx20_4_1_out_26), .a(transmission_1_p4), .y(O_DATA[0]));  // open: x0
  mx2_1 mx2_1_21 (.x1(mx20_4_1_out_27), .a(transmission_1_p4), .y(O_DATA[1]));  // open: x0
  mx2_1 mx2_1_22 (.x1(mx20_4_1_out_28), .a(transmission_1_p4), .y(O_DATA[2]));  // open: x0
  mx2_1 mx2_1_23 (.x1(mx20_4_1_out_29), .a(transmission_1_p4), .y(O_DATA[3]));  // open: x0

  // Notes on the sheet:
  //   индексы стека
  //   push
  //   если рор, то меняем индекс
  //   это нужно, если get (- четыре входящих бита + top mod 5)
  //   если рор, то порядок сдвинуть по циклу на 1
  //   иначе порядок верный
  //   pop
  //   проверка на то, нужен вывод или нет
  //   проверка на reset
  //   push
endmodule

module dec2_4 (
  input  in_1,
  input  in_2,
  output out_3,
  output out_4,
  output out_5,
  output out_6
);

  wire not_1_out, not_2_out;

  not not_1 (not_1_out, in_1);
  not not_2 (not_2_out, in_2);
  and and_1 (out_3, not_1_out, not_2_out);
  and and_2 (out_4, in_1, not_2_out);
  and and_3 (out_5, in_2, not_1_out);
  and and_4 (out_6, in_1, in_2);
endmodule

module mod5_4bit (
  input  q0,
  input  q1,
  input  q2,
  input  q3,
  output out_5,
  output out_6,
  output out_7
);

  wire add1mod5_1_y1, add1mod5_1_y2, add1mod5_2_y1, add1mod5_2_y2, and_1_out, mx2_1_1_y, mx2_1_2_y,
       mx2_1_3_y, mx2_1_4_y, mx2_1_5_y, mx2_1_6_y, mx2_1_7_y, mx2_1_8_y, mx2_1_9_y, xor_1_out, xor_2_out;

  xor xor_1 (xor_1_out, q0, q2);
  xor xor_2 (xor_2_out, q1, q3);
  mx2_1 mx2_1_1 (.x0(1'b0), .x1(1'b1), .a(xor_1_out), .y(mx2_1_1_y));
  mx2_1 mx2_1_2 (.x0(1'b0), .x1(1'b1), .a(xor_2_out), .y(mx2_1_2_y));
  mx2_1 mx2_1_3 (.x0(1'b0), .x1(q0), .a(mx2_1_1_y), .y(mx2_1_3_y));
  mx2_1 mx2_1_4 (.x0(1'b0), .x1(q2), .a(mx2_1_1_y), .y(mx2_1_4_y));
  mx2_1 mx2_1_5 (.x0(1'b0), .x1(q1), .a(mx2_1_2_y), .y(mx2_1_5_y));
  mx2_1 mx2_1_6 (.x0(1'b0), .x1(q3), .a(mx2_1_2_y), .y(mx2_1_6_y));
  add1mod5 add1mod5_1 (.a0(mx2_1_3_y), .a1(1'b1), .b(1'b0), .y1(add1mod5_1_y1), .y2(add1mod5_1_y2));
  mx2_1 mx2_1_7 (.x0(mx2_1_3_y), .x1(add1mod5_1_y1), .a(mx2_1_6_y), .y(mx2_1_7_y));
  mx2_1 mx2_1_8 (.x0(mx2_1_5_y), .x1(add1mod5_2_y1), .a(mx2_1_6_y), .y(mx2_1_8_y));
  mx2_1 mx2_1_9 (.x0(mx2_1_4_y), .x1(add1mod5_2_y2), .a(mx2_1_6_y), .y(mx2_1_9_y));
  add1mod5 add1mod5_2 (.a0(mx2_1_5_y), .a1(1'b1), .b(add1mod5_1_y2), .y1(add1mod5_2_y1), .y2(add1mod5_2_y2));
  and and_1 (and_1_out, mx2_1_8_y, mx2_1_9_y);
  mx2_1 mx2_1_10 (.x0(mx2_1_7_y), .x1(1'b1), .a(and_1_out), .y(out_5));
  mx2_1 mx2_1_11 (.x0(mx2_1_8_y), .x1(1'b0), .a(and_1_out), .y(out_6));
  mx2_1 mx2_1_12 (.x0(mx2_1_9_y), .x1(1'b0), .a(and_1_out), .y(out_7));

  // Notes on the sheet:
  //   первая и третья цифры
  //   вторая и четвертая цифры
endmodule

module c5_3 (
  input  x1,
  input  x2,
  input  x3,
  input  x4,
  input  x5,
  output y1,
  output y2,
  output y3
);

  or or_1 (y1, x2, x4);
  or or_2 (y2, x3, x4);
  or or_3 (y3, x5, x5);
endmodule

module mx20_4 (
  input  in_1,
  input  in_2,
  input  in_3,
  input  in_4,
  input  in_5,
  input  in_6,
  input  in_7,
  input  in_8,
  input  in_9,
  input  in_10,
  input  in_11,
  input  in_12,
  input  in_13,
  input  in_14,
  input  in_15,
  input  in_16,
  input  in_17,
  input  in_18,
  input  in_19,
  input  in_20,
  input  in_21,
  input  in_22,
  input  in_23,
  input  in_24,
  input  in_25,
  output out_26,
  output out_27,
  output out_28,
  output out_29
);

  wire mx2_1_1_y, mx2_1_2_y, mx2_1_3_y, mx2_1_4_y, mx2_1_5_y, mx2_1_6_y, mx2_1_7_y, mx2_1_8_y, mx2_1_9_y,
       mx2_1_10_y, mx2_1_11_y, mx2_1_12_y, mx2_1_13_y, mx2_1_14_y, mx2_1_15_y, mx2_1_16_y;

  mx2_1 mx2_1_1 (.x0(1'b0), .x1(in_1), .a(in_21), .y(mx2_1_1_y));
  mx2_1 mx2_1_2 (.x0(1'b0), .x1(in_2), .a(in_21), .y(mx2_1_2_y));
  mx2_1 mx2_1_3 (.x0(1'b0), .x1(in_3), .a(in_21), .y(mx2_1_3_y));
  mx2_1 mx2_1_4 (.x0(1'b0), .x1(in_4), .a(in_21), .y(mx2_1_4_y));
  mx2_1 mx2_1_5 (.x0(mx2_1_1_y), .x1(in_5), .a(in_22), .y(mx2_1_5_y));
  mx2_1 mx2_1_6 (.x0(mx2_1_2_y), .x1(in_6), .a(in_22), .y(mx2_1_6_y));
  mx2_1 mx2_1_7 (.x0(mx2_1_3_y), .x1(in_7), .a(in_22), .y(mx2_1_7_y));
  mx2_1 mx2_1_8 (.x0(mx2_1_4_y), .x1(in_8), .a(in_22), .y(mx2_1_8_y));
  mx2_1 mx2_1_9 (.x0(mx2_1_5_y), .x1(in_9), .a(in_23), .y(mx2_1_9_y));
  mx2_1 mx2_1_10 (.x0(mx2_1_6_y), .x1(in_10), .a(in_23), .y(mx2_1_10_y));
  mx2_1 mx2_1_11 (.x0(mx2_1_7_y), .x1(in_11), .a(in_23), .y(mx2_1_11_y));
  mx2_1 mx2_1_12 (.x0(mx2_1_8_y), .x1(in_12), .a(in_23), .y(mx2_1_12_y));
  mx2_1 mx2_1_13 (.x0(mx2_1_9_y), .x1(in_13), .a(in_24), .y(mx2_1_13_y));
  mx2_1 mx2_1_14 (.x0(mx2_1_10_y), .x1(in_14), .a(in_24), .y(mx2_1_14_y));
  mx2_1 mx2_1_15 (.x0(mx2_1_11_y), .x1(in_15), .a(in_24), .y(mx2_1_15_y));
  mx2_1 mx2_1_16 (.x0(mx2_1_12_y), .x1(in_16), .a(in_24), .y(mx2_1_16_y));
  mx2_1 mx2_1_17 (.x0(mx2_1_13_y), .x1(in_17), .a(in_25), .y(out_26));
  mx2_1 mx2_1_18 (.x0(mx2_1_14_y), .x1(in_18), .a(in_25), .y(out_27));
  mx2_1 mx2_1_19 (.x0(mx2_1_15_y), .x1(in_19), .a(in_25), .y(out_28));
  mx2_1 mx2_1_20 (.x0(mx2_1_16_y), .x1(in_20), .a(in_25), .y(out_29));
endmodule

module mod5min3 (
  input  in_1,
  input  in_2,
  input  in_3,
  output out_4,
  output out_5,
  output out_6
);

  wire dec3_5_1_y1, dec3_5_1_y2, dec3_5_1_y3, dec3_5_1_y4, dec3_5_1_y5;

  dec3_5 dec3_5_1 (
    .x1(in_1), .x2(in_2), .x3(in_3), .y1(dec3_5_1_y1), .y2(dec3_5_1_y2), .y3(dec3_5_1_y3), .y4(dec3_5_1_y4),
    .y5(dec3_5_1_y5));
  c5_3 c5_3_1 (
    .x1(dec3_5_1_y5), .x2(dec3_5_1_y1), .x3(dec3_5_1_y2), .x4(dec3_5_1_y3), .x5(dec3_5_1_y4), .y1(out_4),
    .y2(out_5), .y3(out_6));

  // Notes on the sheet:
  //   число уже приведено к mod5
endmodule
